# Fritzing sketch schemati (saved by Fritzing 0.9.3b)
breadboards: 1

parts:
  Nokia_5110_LCD_Module1 = Nokia 5110 LCD
  Onderdeel1 = Thumb Joystick
  Onderdeel2 = Arduino Nano (Rev3.0)
  S1 = Pushbutton [package="[THT]"]
  S2 = Pushbutton [package="[THT]"]
  part = Resistor [tolerance=±5% resistance=330 package=THT]
  part_2 = Resistor [tolerance=±5% resistance=1k package=THT]
  Onderdeel4 = Logic Level Converter
  part_3 = Resistor [tolerance=±5% resistance=10k package=THT]
  U1 = microSD Socket [package=usd-socket-pp]
  part_4 = Resistor [tolerance=±5% resistance=1k package=THT]

nets:
  N1: Nokia_5110_LCD_Module1.RST, Nokia_5110_LCD_Module1.RST_(out), part_3.Pin_1
  3.3V: Nokia_5110_LCD_Module1.VCC_(out), Onderdeel2.3V3, Onderdeel4.LV, U1.VCC
  GND: Nokia_5110_LCD_Module1.GND_(out), Onderdeel1.GND, Onderdeel2.GND, S1.Pin_4, S2.Pin_4, Onderdeel4.GND, U1.GND
  N2: Nokia_5110_LCD_Module1.SCE_(out), part_2.Pin_1
  N3: Nokia_5110_LCD_Module1.D/C_(out), Onderdeel4.HV2
  N4: Nokia_5110_LCD_Module1.DN(MODI)_(out), Onderdeel4.HV4, U1.DI
  N5: Nokia_5110_LCD_Module1.SCLK_(out), Onderdeel4.LV1, U1.SCK
  N6: Nokia_5110_LCD_Module1.LED_(out), part.Pin_1
  N7: Onderdeel1.SEL, Onderdeel2.A2
  N8: Onderdeel1.HORZ, Onderdeel2.A0
  N9: Onderdeel1.VERT, Onderdeel2.A1
  5V: Onderdeel1.VCC, Onderdeel2.5V, Onderdeel4.HV
  N10: Onderdeel2.D6, part_4.Pin_0
  N11: Onderdeel2.D7, part_2.Pin_0
  N12: Onderdeel2.D8, part_3.Pin_0
  N13: Onderdeel2.D9, part.Pin_0
  N14: Onderdeel2.D10, Onderdeel4.LV2
  N15: Onderdeel2.D11/MOSI, Onderdeel4.LV4
  N16: Onderdeel2.D12/MISO, Onderdeel4.HV3
  N17: Onderdeel2.A4, S2.Pin_1, S2.Pin_2
  N18: Onderdeel2.A3, S1.Pin_1, S1.Pin_2
  N19: Onderdeel2.D13/SCK, Onderdeel4.HV1
  N20: Onderdeel4.LV3, U1.DO
  N21: U1.CS, part_4.Pin_1

custom parts:
  Nokia 5110 LCD: Nokia 5110 Graphic 84*48 LCD module such as the Sparkfun LCD-10168 or the clones from Ebay. There is example code for the Arduino available from the Sparkfun site in https://learn.sparkfun.com/tutorials/graphic-lcd-hookup-guide This is a 3.3V device, if you are running it from a 5V micro you need a 5V tolorant level translator such as the 74ahc367 to protect the signal imputs. Rafa G. did a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
  Logic Level Converter: Description: If you've ever tried to connect a 3.3V device to a 5V system, you know what a challenge it can be. The SparkFun logic level converter is a small device that safely steps down 5V signals to 3.3V and steps up 3.3V to 5V. This level converter also works with 2.8V and 1.8V devices. Each level converter has the capability of converting 4 pins on the high side to 4 pins on the low side.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
